# Fritzing sketch sketch_ver1 (saved by Fritzing 0.9.3b)
perfboards: 1

parts:
  BAT1 = BC9VPC [package=bc9vpc]
  Debugger1 = Debugger  # not connected
  J5 = female alternating pin header, 5 pins [form="♀ (female)"]  # not connected
  元件1 = Arduino Pro Mini v13  # not connected
  J6 = female alternating pin header, 2 pins [form="♀ (female)"]  # not connected
  J7 = Dagu DGServo 9g header connector (female) [package=THT]  # not connected
  J8 = Dagu DGServo 9g header connector (female) [package=THT]  # not connected
  元件3 = Bluetooth HC-05 Macho  # not connected
  J9 = female pin header, 6 pins [form="♀ (female)"]  # not connected
  J5_2 = double row male pin header, 2 pins [form="♂ (male)"]
  J10 = Basic Servo  # not connected

nets:
  N1: BAT1.V+, J5_2.pin2
  N2: BAT1.V-, J5_2.pin1
