# Fritzing sketch sketch_ver2 (saved by Fritzing 0.9.3b)
perfboards: 2

parts:
  Battery = BC9VPC [package=bc9vpc]
  Debugger1 = Debugger  # not connected
  元件1 = Arduino Pro Mini v13
  toMotor1 = Dagu DGServo 9g header connector (female) [package=THT]  # not connected
  Bluetooth = Bluetooth HC-05 Macho  # not connected
  toBluetooth = female pin header, 6 pins [form="♀ (female)"]  # not connected
  Motor = Basic Servo
  toBattery1 = female alternating pin header, 2 pins [form="♀ (female)"]  # not connected
  toMotor2 = Dagu DGServo 9g header connector (female) [package=THT]  # not connected
  toBattery2 = male alternating pin header, 2 pins [form="♂ (male)"]
  toMotor = male alternating pin header, 3 pins [form="♂ (male)"]
  toBattery3 = female alternating pin header, 2 pins [form="♀ (female)"]
  toMotor3 = Dagu DGServo 9g header connector (female) [package=THT]
  toMotor4 = Dagu DGServo 9g header connector (female) [package=THT]
  toBluetooth1 = female pin header, 6 pins [form="♀ (female)"]
  toArduino = female pin header, 12 pins [form="♀ (female)"]  # not connected
  toArduino1 = female pin header, 12 pins [form="♀ (female)"]  # not connected
  toArduino2 = female pin header, 12 pins [form="♀ (female)"]
  toArduino3 = female pin header, 12 pins [form="♀ (female)"]
  Motor1 = Basic Servo
  toMotor5 = male alternating pin header, 3 pins [form="♂ (male)"]
  toArduino6 = male pin header, 6 pins [form="♂ (male)"]

nets:
  N1: Battery.V+, toBattery2.pin1
  N2: Battery.V-, toBattery2.pin2
  N3: 元件1.DTR, toArduino6.pin1
  N4: 元件1.D0/TX, toArduino6.pin2
  N5: 元件1.D1/RX, toArduino6.pin3
  N6: 元件1.VCC, toArduino6.pin4
  N7: 元件1.GND, toArduino6.pin5, toArduino6.pin6
  N8: Motor.gnd, toMotor.pin3
  N9: Motor.vcc, toMotor.pin2
  N10: Motor.pulse, toMotor.pin1
  N11: toBattery3.pin1, toArduino2.pin2
  N12: toBattery3.pin2, toArduino2.pin1
  N13: toMotor3.gnd, toArduino3.pin10
  N14: toMotor3.Vcc, toArduino3.pin11
  N15: toMotor3.pulse, toArduino3.pin12
  N16: toMotor4.gnd, toArduino3.pin4
  N17: toMotor4.Vcc, toArduino3.pin5
  N18: toMotor4.pulse, toArduino3.pin6
  N19: toBluetooth1.pin1, toArduino2.pin12
  N20: Motor1.gnd, toMotor5.pin3
  N21: Motor1.vcc, toMotor5.pin2
  N22: Motor1.pulse, toMotor5.pin1
